// Digital circuit part_c.dig as structural Verilog
module part_c (
  input  in_0,
  input  in_1,
  input  in_2,
  output out_0
);

  wire fgnfet_1_d, fgnfet_2_d, fgnfet_3_d, fgpfet_1_d, fgpfet_3_d, fgpfet_5_d, fgpfet_7_d, fgpfet_8_d;

  FGNFET fgnfet_1 (.G(in_0), .D(fgnfet_1_d), .S(1'b1));
  FGPFET fgpfet_1 (.G(in_0), .S(1'b0), .D(fgpfet_1_d));
  FGPFET fgpfet_2 (.G(in_1), .S(1'b0), .D(fgpfet_1_d));
  FGNFET fgnfet_2 (.G(in_1), .D(fgnfet_2_d), .S(1'b1));
  FGPFET fgpfet_3 (.G(in_1), .S(1'b0), .D(fgpfet_3_d));
  FGPFET fgpfet_4 (.G(in_2), .S(1'b0), .D(fgpfet_3_d));
  FGNFET fgnfet_3 (.G(in_0), .D(fgnfet_3_d), .S(1'b1));
  FGPFET fgpfet_5 (.G(in_0), .S(1'b0), .D(fgpfet_5_d));
  FGPFET fgpfet_6 (.G(in_2), .S(1'b0), .D(fgpfet_5_d));
  FGNFET fgnfet_4 (.G(in_1), .D(fgpfet_1_d), .S(fgnfet_1_d));
  FGNFET fgnfet_5 (.G(in_2), .D(fgpfet_3_d), .S(fgnfet_2_d));
  FGNFET fgnfet_6 (.G(in_2), .D(fgpfet_5_d), .S(fgnfet_3_d));
  FGPFET fgpfet_7 (.G(fgpfet_1_d), .S(1'b0), .D(fgpfet_7_d));
  FGNFET fgnfet_7 (.G(fgpfet_1_d), .D(out_0), .S(1'b1));
  FGNFET fgnfet_8 (.G(fgpfet_3_d), .D(out_0), .S(1'b1));
  FGNFET fgnfet_9 (.G(fgpfet_5_d), .D(out_0), .S(1'b1));
  FGPFET fgpfet_8 (.G(fgpfet_3_d), .S(fgpfet_7_d), .D(fgpfet_8_d));
  FGPFET fgpfet_9 (.G(fgpfet_5_d), .S(fgpfet_8_d), .D(out_0));

  // Other names for the same wires on the sheet: in_0_tunnel = in_0; in_1_tunnel = in_1; in_2_tunnel = in_2

  // Notes on the sheet:
  //   AND Gate
  //   OR Gate
endmodule

/* Test case part_c_test:
in_0 in_1 in_2 out_0
0 0 0 0
0 0 1 0
0 1 0 0
0 1 1 1
1 0 0 0
1 0 1 1
1 1 0 1
1 1 1 1
*/
