// Digital circuit lab2_part2.dig as structural Verilog
module lab2_part2 (
  input  in0,
  input  in1,
  input  in2,
  input  in3,
  output seg_a,
  output seg_f,
  output seg_b,
  output seg_g,
  output seg_e,
  output seg_c,
  output seg_d,
  output seg_dp,
  output sign_a,
  output sign_f,
  output sign_b,
  output sign_g,
  output sign_e,
  output sign_c,
  output sign_d,
  output sign_dp
);

  wire _0000, _0001, _0010, _0011, _0100, _0101, _0110, _0111, _1000, _1001, _1010, _1011, _1100, _1101,
       _1110, _1111, or_1_out, or_2_out, or_3_out, or_4_out, or_5_out, or_6_out, or_7_out, or_8_out,
       or_9_out, or_10_out, or_11_out, or_12_out, or_13_out, or_14_out;

  Seven_Seg seven_seg_1 (.a(1'b0), .b(1'b0), .c(1'b0), .d(1'b0), .e(1'b0), .f(1'b0), .g(in3), .dp(1'b0));
  Seven_Seg seven_seg_2 (.a(seg_a), .b(seg_b), .c(seg_c), .d(seg_d), .e(seg_e), .f(seg_f), .g(seg_g), .dp(1'b0));
  and and_1 (_0010, ~in3, ~in2, in1, ~in0);  // And
  and and_2 (_1110, in3, in2, in1, ~in0);  // And
  and and_3 (_0011, ~in3, ~in2, in1, in0);  // And
  and and_4 (_0000, ~in3, ~in2, ~in1, ~in0);  // And
  and and_5 (_1101, in3, in2, ~in1, in0);  // And
  and and_6 (_0101, ~in3, in2, ~in1, in0);  // And
  and and_7 (_1011, in3, ~in2, in1, in0);  // And
  and and_8 (_0111, ~in3, in2, in1, in0);  // And
  and and_9 (_1001, in3, ~in2, ~in1, in0);  // And
  and and_10 (_1000, in3, ~in2, ~in1, ~in0);  // And
  and and_11 (_0001, ~in3, ~in2, ~in1, in0);  // And
  and and_12 (_1111, in3, in2, in1, in0);
  and and_13 (_0100, ~in3, in2, ~in1, ~in0);  // And
  and and_14 (_1100, in3, in2, ~in1, ~in0);  // And
  and and_15 (_0110, ~in3, in2, in1, ~in0);  // And
  and and_16 (_1010, in3, ~in2, in1, ~in0);  // And
  or or_1 (or_1_out, _0010, _1110, _0011, _0000, _1101);
  or or_2 (or_2_out, _0101, _1011, _0111, _1001, _1000);
  or or_3 (or_3_out, _0000, _0001, _1111, _0010, _1110);
  or or_4 (or_4_out, _0011, _1101, _0100, _1100, _0111);
  or or_5 (or_5_out, _0000, _0001, _1111, _0101, _1011);
  or or_6 (or_6_out, _0011, _1101, _0100, _1100, _0111);
  or or_7 (or_7_out, _1001, _1000, _0110, _1010);
  or or_8 (or_8_out, _0000, _0010, _1110, _0011, _1101);
  or or_9 (or_9_out, _0101, _1011, _0110, _1010, _1000);
  or or_10 (or_10_out, _0000, _0010, _1110, _0110, _1010);
  or or_11 (or_11_out, _0000, _0100, _1100, _0101, _1011);
  or or_12 (or_12_out, _0110, _1010, _1000);
  or or_13 (or_13_out, _0010, _1110, _0011, _1000, _1101);
  or or_14 (or_14_out, _1100, _0101, _1011, _0110, _1010);
  or or_15 (seg_a, or_1_out, _0110, _1010, or_2_out);
  or or_16 (seg_b, or_3_out, _1001, _1000, or_4_out);
  or or_17 (seg_c, or_5_out, or_6_out, or_7_out);
  or or_18 (seg_d, or_8_out, or_9_out);
  or or_19 (seg_e, or_10_out, _1000);
  or or_20 (seg_f, or_11_out, or_12_out);
  or or_21 (seg_g, or_13_out, _0100, or_14_out);

  assign seg_dp = 1'b0;
  assign sign_a = 1'b0;
  assign sign_b = 1'b0;
  assign sign_c = 1'b0;
  assign sign_d = 1'b0;
  assign sign_dp = 1'b0;
  assign sign_e = 1'b0;
  assign sign_f = 1'b0;
  assign sign_g = in3;

  // Notes on the sheet:
  //   Interface (do not edit the content inside this box)
  //   Outputs:
  //   Inputs
  //   Sign
  //   Decimal Number
  //   Possible 1s and 0s
  //   Doesn't Need to Light Up
  //   Segment A
  //   Segment B
  //   Segment C
  //   Segment D
  //   Segment E
  //   Segment F
  //   Segment G
endmodule

/* Test case:
in3 in2 in1 in0  sign_a sign_b sign_c sign_d sign_e sign_f sign_g  seg_a seg_b seg_c seg_d seg_e seg_f seg_g
 0   0   0   0    0      0      0      0      0      0      0       1     1     1     1     1     1     0
*/
